// Logisim project s-mips.circ as structural Verilog
module S_MIPS_Board (
  input  DESHABILITAR_DISPATCHER,
  output halt
);

  wire button_1_out, CLK, CS, d_ff_1_q, LCLR, LoadRAM, LoadRAMOn, LW, R_R_W, R_W, ram_dispatcher_1_finished,
       RCS, Reset_out, RST, TTY_EN;
  wire [2:0] KDB;
  wire [3:0] LMask, Mask, ram_1_read_time, ram_1_write_time, RMask;
  wire [6:0] KDB_DATA, TTY_DATA;
  wire [15:0] Addr, LAddr, RAddr;
  wire [31:0] I0, I1, I2, I3, LData, ram_1_data_out_0, ram_1_data_out_1, ram_1_data_out_2, ram_1_data_out_3,
       RI0, RI1, RI2, RI3;

  TTY #(.rows(25), .cols(80)) tty_1 (.data(TTY_DATA), .clk(CLK), .we(TTY_EN), .clr(RST));
  not not_1 (LoadRAMOn, ram_dispatcher_1_finished);
  RAM_Dispatcher ram_dispatcher_1 (
    .WriteTime(ram_1_write_time), .Clock(CLK), .Data(LData), .Address(LAddr), .Mask(LMask),
    .Finished(ram_dispatcher_1_finished), .Write(LW), .CLR(LCLR));
  Keyboard #(.buflen(64)) keyboard_1 (.clk(CLK), .re(KDB[0]), .avail(KDB[2]), .data(KDB_DATA));  // open: clr
  RAM ram_1 (
    .Address(RAddr), .Data_Out_0(ram_1_data_out_0), .Data_Out_1(ram_1_data_out_1),
    .Data_Out_2(ram_1_data_out_2), .Data_Out_3(ram_1_data_out_3), .Data_In_0(RI0), .Data_In_1(RI1),
    .Data_In_2(RI2), .Data_In_3(RI3), .Mask(RMask), .nRead_Write(R_R_W), .Chip_Select(RCS),
    .Read_Time(ram_1_read_time), .Reset(button_1_out), .Write_Time(ram_1_write_time));
  Button button_1 (.out(button_1_out));
  D_Flip_Flop d_ff_1 (.clk(CLK), .D(1'b1), .Q(d_ff_1_q), .reset(Reset_out));  // open: Qn, preset, en
  Button Reset (.out(Reset_out));
  S_MIPS s_mips_1 (
    .Kbd_Enable(KDB[0]), .Address(Addr), .Kbd_Clear(KDB[1]), .Kbd_Available(KDB[2]), .RAM_In_0(I0),
    .Kbd_ASCII_Data(KDB_DATA), .RAM_In_1(I1), .TTY_Enable(TTY_EN), .RAM_In_2(I2), .RAM_In_3(I3),
    .TTY_ASCII_Data(TTY_DATA), .Reset(RST), .RAM_Out_0(ram_1_data_out_0), .Clock(CLK),
    .RAM_Out_1(ram_1_data_out_1), .Stop(halt), .RAM_Out_2(ram_1_data_out_2), .RAM_Out_3(ram_1_data_out_3),
    .Mask(Mask), .Read_Time(ram_1_read_time), .Write_Time(ram_1_write_time), .nRead_Write(R_W),
    .Chip_Select(CS));
  D_Flip_Flop d_ff_2 (.clk(CLK), .D(d_ff_1_q), .Qn(LCLR), .reset(Reset_out));  // open: Q, preset, en
  or or_1 (RST, LCLR, LoadRAM);
  Clock clock_1 (.out(CLK));
  Multiplexer #(.width(32), .enable("false")) multiplexer_1 (.in0(I0), .in1(LData), .out(RI0), .sel(LoadRAM));
  Multiplexer #(.width(32), .enable("false")) multiplexer_2 (.in0(I1), .in1(LData), .out(RI1), .sel(LoadRAM));
  Multiplexer #(.width(32), .enable("false")) multiplexer_3 (.in0(I2), .in1(LData), .out(RI2), .sel(LoadRAM));
  Multiplexer #(.width(32), .enable("false")) multiplexer_4 (.in0(I3), .in1(LData), .out(RI3), .sel(LoadRAM));
  and and_1 (LoadRAM, ~DESHABILITAR_DISPATCHER, LoadRAMOn);  // AND_Gate
  Multiplexer #(.width(16), .enable("false")) multiplexer_5 (.in0(Addr), .in1(LAddr), .out(RAddr), .sel(LoadRAM));
  Multiplexer #(.width(4), .enable("false")) multiplexer_6 (.in0(Mask), .in1(LMask), .out(RMask), .sel(LoadRAM));
  Multiplexer #(.enable("false")) multiplexer_7 (.in0(CS), .in1(LW), .out(RCS), .sel(LoadRAM));
  Multiplexer #(.enable("false")) multiplexer_8 (.in0(R_W), .in1(LW), .out(R_R_W), .sel(LoadRAM));

  // Notes on the sheet:
  //   NO MODIFICAR
  //   Keyboard
endmodule

module RAM (
  input  [15:0] Address,
  input  [31:0] Data_In_0,
  input  [31:0] Data_In_1,
  input  [31:0] Data_In_2,
  input  [31:0] Data_In_3,
  input  [3:0] Mask,
  input  nRead_Write,
  input  Chip_Select,
  input  Reset,
  output [31:0] Data_Out_0,
  output [31:0] Data_Out_1,
  output [31:0] Data_Out_2,
  output [31:0] Data_Out_3,
  output [3:0] Read_Time,
  output [3:0] Write_Time
);

  wire and_2_out, and_3_out, and_4_out, and_5_out, and_6_out, and_7_out, and_8_out, and_9_out, Changed, CLK,
       comparator_2_eq, comparator_3_eq, comparator_4_eq, comparator_5_eq, comparator_6_eq, Count,
       demultiplexer_3_out0, Idle, Idle_q, Load, Load0, Load1, nand_1_out, or_1_out, or_2_out, or_3_out,
       or_4_out, or_5_out, or_6_out, or_7_out, or_8_out, or_9_out, or_10_out, Proc_q, Update_Mem, Zero_Time;
  wire [3:0] counter_1_q, multiplexer_1_out, subtractor_1_out;
  wire [31:0] register_1_q, register_2_q, register_3_q, register_4_q, register_5_q;

  // Probe on 4'b0011
  // Probe on 4'b0010
  Multiplexer #(.width(4), .enable("false")) multiplexer_1 (
    .in0(4'b0011), .in1(4'b0010), .out(multiplexer_1_out), .sel(nRead_Write));
  or or_1 (or_1_out, Idle, Update_Mem);
  or or_2 (or_2_out, ~Chip_Select, Reset);  // OR_Gate
  Subtractor #(.width(4)) subtractor_1 (.a(multiplexer_1_out), .b(4'b0010), .out(subtractor_1_out));  // open: bin, bout
  D_Flip_Flop u_Idle (.clk(CLK), .D(or_1_out), .Q(Idle_q), .preset(or_2_out));  // open: Qn, en, reset
  Demultiplexer #(.enable("false")) demultiplexer_1 (.out0(Idle), .out1(Load0), .in(Idle_q), .sel(Changed));
  // Probe on counter_1_q
  Counter #(.width(4), .max('hf)) counter_1 (
    .load(Load), .D(subtractor_1_out), .count(Count), .Q(counter_1_q), .clk(CLK), .clr(or_3_out));  // open: carry
  or or_3 (or_3_out, ~Chip_Select, Reset);  // OR_Gate
  Comparator #(.width(4), .mode("unsigned")) comparator_1 (
    .a(4'b0000), .b(counter_1_q), .eq(Zero_Time));  // open: gt, lt
  or or_4 (or_4_out, Count, Load0, Load1);
  Register #(.width(32)) register_1 (.D(Data_In_0), .en(Chip_Select), .Q(register_1_q), .clk(CLK), .clr(or_5_out));
  or or_5 (or_5_out, ~Chip_Select, Reset);  // OR_Gate
  Register #(.width(32)) register_2 (.D(Data_In_1), .en(Chip_Select), .Q(register_2_q), .clk(CLK), .clr(or_6_out));
  or or_6 (or_6_out, ~Chip_Select, Reset);  // OR_Gate
  Register #(.width(32)) register_3 (.D(Data_In_2), .en(Chip_Select), .Q(register_3_q), .clk(CLK), .clr(or_7_out));
  or or_7 (or_7_out, ~Chip_Select, Reset);  // OR_Gate
  Register #(.width(32)) register_4 (.D(Data_In_3), .en(Chip_Select), .Q(register_4_q), .clk(CLK), .clr(or_8_out));
  or or_8 (or_8_out, ~Chip_Select, Reset);  // OR_Gate
  Register #(.width(32)) register_5 (
    .D({{11{1'b1}}, nRead_Write, Mask, Address}), .en(Chip_Select), .Q(register_5_q), .clk(CLK),
    .clr(or_9_out));
  or or_9 (or_9_out, ~Chip_Select, Reset);  // OR_Gate
  D_Flip_Flop Proc (.clk(CLK), .D(or_4_out), .Q(Proc_q), .reset(or_10_out));  // open: Qn, preset, en
  or or_10 (or_10_out, ~Chip_Select, Reset);  // OR_Gate
  Demultiplexer #(.enable("false")) demultiplexer_2 (
    .out0(Count), .out1(Update_Mem), .in(demultiplexer_3_out0), .sel(Zero_Time));
  Demultiplexer #(.enable("false")) demultiplexer_3 (
    .out0(demultiplexer_3_out0), .out1(Load1), .in(Proc_q), .sel(Changed));
  Clock clock_1 (.out(CLK));
  Comparator #(.width(32)) comparator_2 (.a(register_1_q), .b(Data_In_0), .eq(comparator_2_eq));  // open: gt, lt
  Comparator #(.width(32)) comparator_3 (.a(register_2_q), .b(Data_In_1), .eq(comparator_3_eq));  // open: gt, lt
  Comparator #(.width(32)) comparator_4 (.a(register_3_q), .b(Data_In_2), .eq(comparator_4_eq));  // open: gt, lt
  Comparator #(.width(32)) comparator_5 (.a(register_4_q), .b(Data_In_3), .eq(comparator_5_eq));  // open: gt, lt
  Comparator #(.width(32)) comparator_6 (
    .a(register_5_q), .b({{11{1'b1}}, nRead_Write, Mask, Address}), .eq(comparator_6_eq));  // open: gt, lt
  nand nand_1 (nand_1_out, comparator_6_eq, comparator_2_eq, comparator_3_eq, comparator_4_eq, comparator_5_eq);
  and and_1 (Changed, nand_1_out, Chip_Select);
  or or_11 (Load, Count, Load1, Load0);
  and and_2 (and_2_out, Mask[0], Update_Mem, nRead_Write);
  and and_3 (and_3_out, Mask[1], Update_Mem, nRead_Write);
  and and_4 (and_4_out, Mask[2], Update_Mem, nRead_Write);
  and and_5 (and_5_out, Mask[3], Update_Mem, nRead_Write);
  RAM_part #(.addrWidth(16), .dataWidth(32), .bus("separate")) ram_1 (
    .addr(Address), .din(Data_In_0), .data(Data_Out_0), .str(and_2_out), .sel(Chip_Select), .clk(CLK),
    .ld(and_6_out), .clr(Reset));
  and and_6 (and_6_out, ~nRead_Write, Idle);  // AND_Gate
  RAM_part #(.addrWidth(16), .dataWidth(32), .bus("separate")) ram_2 (
    .addr(Address), .din(Data_In_1), .data(Data_Out_1), .str(and_3_out), .sel(Chip_Select), .clk(CLK),
    .ld(and_7_out), .clr(Reset));
  and and_7 (and_7_out, ~nRead_Write, Idle);  // AND_Gate
  RAM_part #(.addrWidth(16), .dataWidth(32), .bus("separate")) ram_3 (
    .addr(Address), .din(Data_In_2), .data(Data_Out_2), .str(and_4_out), .sel(Chip_Select), .clk(CLK),
    .ld(and_8_out), .clr(Reset));
  and and_8 (and_8_out, ~nRead_Write, Idle);  // AND_Gate
  RAM_part #(.addrWidth(16), .dataWidth(32), .bus("separate")) ram_4 (
    .addr(Address), .din(Data_In_3), .data(Data_Out_3), .str(and_5_out), .sel(Chip_Select), .clk(CLK),
    .ld(and_9_out), .clr(Reset));
  and and_9 (and_9_out, ~nRead_Write, Idle);  // AND_Gate

  assign Read_Time = 4'b0011;
  assign Write_Time = 4'b0010;

  // Other names for the same wires on the sheet: M0 = Mask[0]; M1 = Mask[1]; M2 = Mask[2]; M3 = Mask[3];
  //   RW = nRead_Write; CLR = Reset; CS = Chip_Select; Load2 = Count

  // Notes on the sheet:
  //   NO MODIFICAR
  //   excepto quizás los valores RT y WT
  //   BANK0
  //   BANK1
  //   BANK2
  //   BANK3
endmodule

module S_MIPS (
  input  Kbd_Available,
  input  [6:0] Kbd_ASCII_Data,
  input  [31:0] RAM_Out_0,
  input  [31:0] RAM_Out_1,
  input  Reset,
  input  [31:0] RAM_Out_2,
  input  Clock,
  input  [31:0] RAM_Out_3,
  input  [3:0] Read_Time,
  input  [3:0] Write_Time,
  output Kbd_Enable,
  output [15:0] Address,
  output Kbd_Clear,
  output TTY_Enable,
  output [6:0] TTY_ASCII_Data,
  output Stop,
  output [31:0] RAM_In_0,
  output [31:0] RAM_In_1,
  output [31:0] RAM_In_2,
  output [31:0] RAM_In_3,
  output [3:0] Mask,
  output nRead_Write,
  output Chip_Select
);


  // Other names for the same wires on the sheet: CLK = Clock; CLR = Reset; CS = Chip_Select;
  //   KBD_AVAIL = Kbd_Available; KBD_CLR = Kbd_Clear; KBD_DATA[6:0] = Kbd_ASCII_Data; RAM_A[15:0] = Address;
  //   RAM_INPUT_0[31:0] = RAM_In_0; RAM_INPUT_1[31:0] = RAM_In_1; RAM_INPUT_2[31:0] = RAM_In_2;
  //   RAM_INPUT_3[31:0] = RAM_In_3; RAM_MASK[3:0] = Mask; RAM_OUTPUT_0[31:0] = RAM_Out_0;
  //   RAM_OUTPUT_1[31:0] = RAM_Out_1; RAM_OUTPUT_2[31:0] = RAM_Out_2; RAM_OUTPUT_3[31:0] = RAM_Out_3;
  //   RW = nRead_Write; TTY_DATA[6:0] = TTY_ASCII_Data

  // Notes on the sheet:
  //   RAM ADDRESS
  //   DATA FROM RAM
  //   DATA TO RAM
  //   DATA WRITE MASK
  //   RAM TIMING
  //   RAM CONTROL
  //   KEYBOARD
  //   TTY
  //   SEQUENCING
endmodule

module RAM_Dispatcher (
  input  [3:0] WriteTime,
  input  Clock,
  input  CLR,
  output [31:0] Data,
  output [15:0] Address,
  output [3:0] Mask,
  output Finished,
  output Write
);

  wire demultiplexer_2_out1, demultiplexer_3_out1, End, IDLE_q, IncAddr, Load, or_1_out, or_2_out, While_q,
       WriteEnd;
  wire [3:0] counter_1_q;
  wire [31:0] CurrentAddress_q;

  Counter #(.width(32), .max('hffffffff)) CurrentAddress (
    .count(IncAddr), .Q({CurrentAddress_q[31:18], Address, CurrentAddress_q[1:0]}), .clk(Clock), .clr(CLR));  // open: load, D, carry
  or or_1 (or_1_out, IncAddr, demultiplexer_3_out1, Finished);
  D_Flip_Flop IDLE (.clk(Clock), .D(or_1_out), .Q(IDLE_q), .preset(CLR));  // open: Qn, en, reset
  Demultiplexer #(.enable("false")) demultiplexer_1 (.out0(Load), .out1(Finished), .in(IDLE_q), .sel(End));
  D_Flip_Flop While (.clk(Clock), .D(or_2_out), .Q(While_q), .reset(CLR));  // open: Qn, preset, en
  or or_2 (or_2_out, Write, Load);
  RAM_part #(.addrWidth(18), .dataWidth(32)) ram_1 (
    .addr({Address, CurrentAddress_q[1:0]}), .data(Data), .clk(Clock));  // open: sel, ld, clr
  Demultiplexer #(.enable("false")) demultiplexer_2 (
    .out0(Write), .out1(demultiplexer_2_out1), .in(While_q), .sel(WriteEnd));
  Decoder #(.select(2)) decoder_1 (
    .out0(Mask[0]), .out1(Mask[1]), .out2(Mask[2]), .out3(Mask[3]), .sel(CurrentAddress_q[1:0]));  // open: en
  Demultiplexer #(.enable("false")) demultiplexer_3 (
    .out0(IncAddr), .out1(demultiplexer_3_out1), .in(demultiplexer_2_out1), .sel(End));
  Counter #(.width(4), .max('hf)) counter_1 (
    .load(Load), .D(WriteTime), .count(Write), .Q(counter_1_q), .clk(Clock));  // open: carry, clr
  Comparator #(.width(32)) comparator_1 (.a(Data), .b({32{1'b1}}), .eq(End));  // open: gt, lt
  Comparator #(.width(4)) comparator_2 (.a(4'b0000), .b(counter_1_q), .eq(WriteEnd));  // open: gt, lt

  // Other names for the same wires on the sheet: CLK = Clock; Count = Write; WT[3:0] = WriteTime
endmodule

module multiplier (
  input  [31:0] in_1,
  input  in_2,
  input  [31:0] in_3,
  output [31:0] Output,
  output [31:0] Output_2
);

  wire adder_1_cout, adder_3_cout, adder_5_cout, and_1_out, c1, c2, ca, cb;
  wire [31:0] a_2, a_cb, adder_1_out, adder_2_out, adder_3_out, adder_4_out, and_2_out, and_3_out, b_2, b_ca,
       bit_extender_1_out, bit_extender_2_out, c_ab, HI, HIU, LO, LOU, multiplier_2_cout, multiplier_2_out,
       shift_left_2_out_3, shift_left_3_out_3, shift_left_4_out_3, shift_left_out_3;

  SHR shr_1 (.in_1(in_1), .out_3(a_2), .Output(ca), .in_2(1'b0));
  and and_1 (and_1_out, ca, cb);
  assign bit_extender_1_out = {{31{cb}}, cb};  // Bit_Extender bit_extender_1
  assign bit_extender_2_out = {{31{ca}}, ca};  // Bit_Extender bit_extender_2
  assign c_ab = {{31{1'b0}}, and_1_out};  // Bit_Extender bit_extender_3
  assign and_2_out = a_2 & bit_extender_1_out;  // AND_Gate and_2, 32 bits wide
  assign and_3_out = b_2 & bit_extender_2_out;  // AND_Gate and_3, 32 bits wide
  SHR shr_2 (.in_1(in_3), .out_3(b_2), .Output(cb), .in_2(1'b0));
  SHL shl_1 (.in_1(and_2_out), .out_3(a_cb), .in_2(1'b0));  // open: Output
  SHL shl_2 (.in_1(and_3_out), .out_3(b_ca), .in_2(1'b0));  // open: Output
  Multiplier #(.width(32)) multiplier_1 (.a(in_1), .b(in_3), .out(LO), .cout(HI));  // open: cin
  Multiplier #(.width(32)) multiplier_2 (
    .a(a_2), .b(b_2), .out(multiplier_2_out), .cout(multiplier_2_cout));  // open: cin
  SHL shift_left (.in_1(multiplier_2_out), .out_3(shift_left_out_3), .Output(c1), .in_2(1'b0));
  SHL shift_left_2 (.in_1(multiplier_2_cout), .out_3(shift_left_2_out_3), .in_2(c1));  // open: Output
  SHL shift_left_3 (.in_1(shift_left_out_3), .out_3(shift_left_3_out_3), .Output(c2), .in_2(1'b0));
  SHL shift_left_4 (.in_1(shift_left_2_out_3), .out_3(shift_left_4_out_3), .in_2(c2));  // open: Output
  // Probe on HIU
  Multiplexer #(.width(32), .enable("false")) multiplexer_1 (.in0(HIU), .in1(HI), .out(Output), .sel(in_2));
  Multiplexer #(.width(32), .enable("false")) multiplexer_2 (.in0(LOU), .in1(LO), .out(Output_2), .sel(in_2));
  Adder #(.width(32)) adder_1 (.a(shift_left_3_out_3), .b(a_cb), .out(adder_1_out), .cout(adder_1_cout));  // open: cin
  Adder #(.width(32)) adder_2 (
    .a(shift_left_4_out_3), .b({32{1'b0}}), .out(adder_2_out), .cin(adder_1_cout));  // open: cout
  Adder #(.width(32)) adder_3 (.a(adder_1_out), .b(b_ca), .out(adder_3_out), .cout(adder_3_cout));  // open: cin
  Adder #(.width(32)) adder_4 (.a(adder_2_out), .b({32{1'b0}}), .out(adder_4_out), .cin(adder_3_cout));  // open: cout
  Adder #(.width(32)) adder_5 (.a(adder_3_out), .b(c_ab), .out(LOU), .cout(adder_5_cout));  // open: cin
  Adder #(.width(32)) adder_6 (.a(adder_4_out), .b({32{1'b0}}), .out(HIU), .cin(adder_5_cout));  // open: cout

  // Other names for the same wires on the sheet: a[31:0] = in_1; b[31:0] = in_3; sign = in_2
endmodule

module SHR (
  input  [31:0] in_1,
  input  in_2,
  output [31:0] out_3,
  output Output
);


  assign out_3 = {in_2, in_1[31:1]};
  assign Output = in_1[0];

  // Other names for the same wires on the sheet: a[31:0] = in_1; a_2[31:0] = {in_2, in_1[31:1]}
endmodule

module SHL (
  input  [31:0] in_1,
  input  in_2,
  output [31:0] out_3,
  output Output
);


  assign out_3 = {in_1[30:0], in_2};
  assign Output = in_1[31];

  // Other names for the same wires on the sheet: a[31:0] = in_1; a_2[31:0] = {in_1[30:0], in_2}
endmodule

module divider (
  input  [31:0] in_1,
  input  in_2,
  input  [31:0] in_3,
  output [31:0] out_4,
  output [31:0] out_5
);

  wire comparator_1_gt, neg_a, neg_b, neg_div, not_1_out, R_plus;
  wire [0:0] and_4_out;
  wire [31:0] abs_a, abs_b, abs_div, adder_1_out, adder_2_out, negator_1_out, negator_2_out, negator_3_out,
       negator_4_out, R, res, undriven;

  // Probe on in_1
  Negator #(.width(32)) negator_1 (.in(in_1), .out(negator_1_out));
  Negator #(.width(32)) negator_2 (.in(in_3), .out(negator_2_out));
  // Probe on in_3
  and and_1 (neg_a, in_1[31], in_2);
  and and_2 (neg_b, in_2, in_3[31]);
  Multiplexer #(.width(32), .enable("false")) multiplexer_1 (.in0(in_1), .in1(negator_1_out), .out(abs_a), .sel(neg_a));
  Multiplexer #(.width(32), .enable("false")) multiplexer_2 (.in0(in_3), .in1(negator_2_out), .out(abs_b), .sel(neg_b));
  Divider #(.width(32)) divider_1 (.a(abs_a), .b(abs_b), .out(res), .rem(R));  // open: upper
  not not_1 (not_1_out, neg_b);
  Comparator #(.width(32), .mode("unsigned")) comparator_1 (
    .a(undriven), .b({32{1'b0}}), .gt(comparator_1_gt));  // open: eq, lt
  and and_3 (R_plus, neg_a, not_1_out, comparator_1_gt);
  // Probe on out_4
  xor xor_1 (neg_div, neg_a, neg_b);
  Adder #(.width(32)) adder_1 (.a(res), .b(32'h1), .out(adder_1_out));  // open: cin, cout
  Multiplexer #(.width(32), .enable("false")) multiplexer_3 (.in0(res), .in1(adder_1_out), .out(abs_div), .sel(R_plus));
  // Probe on out_5
  Multiplexer #(.width(32), .enable("false")) multiplexer_4 (
    .in0(abs_div), .in1(negator_3_out), .out(out_4), .sel(neg_div));
  Negator #(.width(32)) negator_3 (.in(abs_div), .out(negator_3_out));
  Negator #(.width(32)) negator_4 (.in(R), .out(negator_4_out));
  Adder #(.width(32)) adder_2 (.a(negator_4_out), .b(in_3), .out(adder_2_out));  // open: cin, cout
  Multiplexer #(.select(2), .width(32), .enable("false")) multiplexer_5 (
    .in0(R), .in1(negator_4_out), .in2(adder_2_out), .out(out_5), .sel({R_plus, and_4_out[0]}));  // open: in3
  and and_4 (and_4_out[0], neg_a, neg_b);

  // Other names for the same wires on the sheet: a[31:0] = in_1; b[31:0] = in_3; div[31:0] = out_4;
  //   remainder[31:0] = out_5; sign = in_2
endmodule

module ALU (
  input  in_1,
  input  in_2,
  input  [31:0] Input,
  input  [31:0] Input_2,
  input  [3:0] in_5,
  output [31:0] Output,
  output [31:0] Output_2,
  output [31:0] Output_3
);

  wire div, enable, mul;
  wire [31:0] add, \and , div_rem, div_res, mult_high, mult_low, multiplexer_2_out, multiplexer_3_out,
       \nand , \nor , \or , slt, sub, \xor ;

  assign \and  = Input & Input_2;  // AND_Gate and_1, 32 bits wide
  assign \or  = Input | Input_2;  // OR_Gate or_1, 32 bits wide
  assign \nand  = ~(Input & Input_2);  // NAND_Gate nand_1, 32 bits wide
  assign \nor  = ~(Input | Input_2);  // NOR_Gate nor_1, 32 bits wide
  assign \xor  = Input ^ Input_2;  // XOR_Gate xor_1, 32 bits wide
  Adder #(.width(32)) adder_1 (.a(Input), .b(Input_2), .out(add));  // open: cin, cout
  Subtractor #(.width(32)) subtractor_1 (.a(Input), .b(Input_2), .out(sub));  // open: bin, bout
  Multiplexer #(.select(4), .width(32), .enable("false")) multiplexer_1 (
    .in0(add), .in1(sub), .in4(slt), .in5(\and ), .in6(\or ), .in7(\nor ), .in8(\xor ), .out(Output),
    .sel(in_5));  // open: in2, in3, in9, in10, in11, in12, in13, in14, in15
  comparator comparator_1 (.in_1(Input), .in_2(in_1), .in_3(Input_2), .Output(slt));
  divider divider_1 (.in_1(Input), .in_2(in_1), .in_3(Input_2), .out_4(div_res), .out_5(div_rem));
  multiplier multiplier_1 (.in_1(Input), .in_2(in_1), .in_3(Input_2), .Output(mult_high), .Output_2(mult_low));
  or or_2 (enable, mul, div);
  and and_2 (mul, ~in_5[0], in_5[1], ~in_5[2], ~in_5[3]);  // AND_Gate
  and and_3 (div, in_5[0], in_5[1], ~in_5[2], ~in_5[3]);  // AND_Gate
  Multiplexer #(.width(32), .enable("false")) multiplexer_2 (
    .in0(mult_low), .in1(div_res), .out(multiplexer_2_out), .sel(div));
  Multiplexer #(.width(32), .enable("false")) multiplexer_3 (
    .in0(mult_high), .in1(div_rem), .out(multiplexer_3_out), .sel(div));
  Register #(.width(32)) register_1 (.D(multiplexer_2_out), .en(enable), .Q(Output_2), .clk(in_2));  // open: clr
  Register #(.width(32)) register_2 (.D(multiplexer_3_out), .en(enable), .Q(Output_3), .clk(in_2));  // open: clr

  // Other names for the same wires on the sheet: a[31:0] = Input; b[31:0] = Input_2; clock = in_2;
  //   HI[31:0] = Output_3; LO[31:0] = Output_2; _0 = in_5[0]; selector[3:0] = in_5; _1 = in_5[1]; _2 = in_5[2];
  //   _3 = in_5[3]; sign = in_1
endmodule

module comparator (
  input  [31:0] in_1,
  input  in_2,
  input  [31:0] in_3,
  output [31:0] Output
);

  wire multiplexer_1_out, slt, sltu;

  Comparator #(.width(32)) comparator_1 (.a(in_1), .b(in_3), .lt(slt));  // open: gt, eq
  Comparator #(.width(32), .mode("unsigned")) comparator_2 (.a(in_1), .b(in_3), .lt(sltu));  // open: gt, eq
  Multiplexer #(.enable("false")) multiplexer_1 (.in0(slt), .in1(sltu), .out(multiplexer_1_out), .sel(in_2));
  assign Output = {{31{1'b0}}, multiplexer_1_out};  // Bit_Extender bit_extender_1

  // Other names for the same wires on the sheet: a[31:0] = in_1; b[31:0] = in_3; sign = in_2
endmodule

module ALU_selector (
  input  in_1,
  input  in_2,
  input  in_3,
  input  in_4,
  input  in_5,
  input  in_6,
  input  in_7,
  input  in_8,
  input  in_9,
  input  in_10,
  input  in_11,
  input  in_12,
  input  in_13,
  input  in_14,
  input  in_15,
  input  in_16,
  input  in_17,
  input  in_18,
  output sign,
  output I,
  output ALU,
  output [3:0] selector
);

  wire AND, DIV, MUL, OR, SLT, SLTI;

  or or_1 (MUL, in_3, in_4);
  or or_2 (DIV, in_5, in_6);
  or or_3 (SLT, in_7, in_8);
  or or_4 (SLTI, in_14, in_15);
  or or_5 (selector[0], in_2, DIV, AND, in_11);
  or or_6 (AND, in_9, in_16);
  or or_7 (OR, in_10, in_17);
  or or_8 (selector[3], in_12, in_18);
  or or_9 (selector[1], MUL, DIV, OR, in_11);
  or or_10 (selector[2], SLT, SLTI, OR, AND, in_11);
  or or_11 (sign, in_3, in_5, in_7, in_14);
  or or_12 (I, in_13, SLTI, in_16, in_17, in_18);
  or or_13 (ALU, selector[0], selector[1], selector[2], selector[3], in_1);

  // Other names for the same wires on the sheet: add = in_1; addi = in_13; and_t = in_9; andi = in_16; div_t = in_5;
  //   divu = in_6; mul_t = in_3; mulu = in_4; nor = in_11; or_t = in_10; ori = in_17; _0 = selector[0];
  //   _1 = selector[1]; _2 = selector[2]; _3 = selector[3]; XOR = selector[3]; slt_t = in_7; slti_t = in_14;
  //   sltiu = in_15; sltu = in_8; sub = in_2; xor_t = in_12; xori = in_18
endmodule

module register_file (
  input  in_1,
  input  in_2,
  input  in_3,
  input  [31:0] in_4,
  input  in_5,
  input  in_6,
  input  in_7,
  input  [4:0] in_8,
  input  [4:0] in_9,
  input  [4:0] in_10,
  output [31:0] Output,
  output [31:0] Output_2,
  output [31:0] Output_3
);

  wire L0, L1, L2, L3, L4, L5, L6, L7, L8, L9, L10, L11, L12, L13, L14, L15, L16, L17, L18, L19, L20, L21,
       L22, L23, L24, L25, L26, L27, L28, L29, L30, L31, or_1_out, or_2_out;
  wire [31:0] adder_1_out, inputSP, multiplexer_3_out, out0, out1, out2, out3, out4, out5, out6, out7, out8,
       out9, out10, out11, out12, out13, out14, out15, out16, out17, out18, out19, out20, out21, out22,
       out23, out24, out25, out26, out27, out28, out29, out30, subtractor_1_out;

  Demultiplexer #(.select(5), .enable("false")) demultiplexer_1 (
    .out0(L0), .out1(L1), .out2(L2), .out3(L3), .out4(L4), .out5(L5), .out6(L6), .out7(L7), .out8(L8),
    .out9(L9), .out10(L10), .out11(L11), .out12(L12), .out13(L13), .out14(L14), .out15(L15), .out16(L16),
    .out17(L17), .out18(L18), .out19(L19), .out20(L20), .out21(L21), .out22(L22), .out23(L23), .out24(L24),
    .out25(L25), .out26(L26), .out27(L27), .out28(L28), .out29(L29), .out30(L30), .in(in_2), .sel(in_8));  // open: out31
  Register #(.width(32)) register_1 (.D({32{1'b0}}), .en(L0), .Q(out0), .clk(in_5), .clr(in_1));
  Register #(.width(32)) register_2 (.D(in_4), .en(L8), .Q(out8), .clk(in_5), .clr(in_1));
  Register #(.width(32)) register_3 (.D(in_4), .en(L16), .Q(out16), .clk(in_5), .clr(in_1));
  Register #(.width(32)) register_4 (.D(in_4), .en(L24), .Q(out24), .clk(in_5), .clr(in_1));
  Register #(.width(32)) register_5 (.D(in_4), .en(L1), .Q(out1), .clk(in_5), .clr(in_1));
  Register #(.width(32)) register_6 (.D(in_4), .en(L9), .Q(out9), .clk(in_5), .clr(in_1));
  Register #(.width(32)) register_7 (.D(in_4), .en(L17), .Q(out17), .clk(in_5), .clr(in_1));
  Register #(.width(32)) register_8 (.D(in_4), .en(L25), .Q(out25), .clk(in_5), .clr(in_1));
  Multiplexer #(.select(5), .width(32), .enable("false")) multiplexer_1 (
    .in0(out0), .in1(out1), .in2(out2), .in3(out3), .in4(out4), .in5(out5), .in6(out6), .in7(out7),
    .in8(out8), .in9(out9), .in10(out10), .in11(out11), .in12(out12), .in13(out13), .in14(out14),
    .in15(out15), .in16(out16), .in17(out17), .in18(out18), .in19(out19), .in20(out20), .in21(out21),
    .in22(out22), .in23(out23), .in24(out24), .in25(out25), .in26(out26), .in27(out27), .in28(out28),
    .in29(out29), .in30(out30), .in31(Output_3), .out(Output), .sel(in_9));
  Register #(.width(32)) register_9 (.D(in_4), .en(L2), .Q(out2), .clk(in_5), .clr(in_1));
  Register #(.width(32)) register_10 (.D(in_4), .en(L10), .Q(out10), .clk(in_5), .clr(in_1));
  Register #(.width(32)) register_11 (.D(in_4), .en(L18), .Q(out18), .clk(in_5), .clr(in_1));
  Register #(.width(32)) register_12 (.D(in_4), .en(L26), .Q(out26), .clk(in_5), .clr(in_1));
  Register #(.width(32)) register_13 (.D(in_4), .en(L3), .Q(out3), .clk(in_5), .clr(in_1));
  Register #(.width(32)) register_14 (.D(in_4), .en(L11), .Q(out11), .clk(in_5), .clr(in_1));
  Register #(.width(32)) register_15 (.D(in_4), .en(L19), .Q(out19), .clk(in_5), .clr(in_1));
  Register #(.width(32)) register_16 (.D(in_4), .en(L27), .Q(out27), .clk(in_5), .clr(in_1));
  Multiplexer #(.select(5), .width(32), .enable("false")) multiplexer_2 (
    .in0(out0), .in1(out1), .in2(out2), .in3(out3), .in4(out4), .in5(out5), .in6(out6), .in7(out7),
    .in8(out8), .in9(out9), .in10(out10), .in11(out11), .in12(out12), .in13(out13), .in14(out14),
    .in15(out15), .in16(out16), .in17(out17), .in18(out18), .in19(out19), .in20(out20), .in21(out21),
    .in22(out22), .in23(out23), .in24(out24), .in25(out25), .in26(out26), .in27(out27), .in28(out28),
    .in29(out29), .in30(out30), .in31(Output_3), .out(Output_2), .sel(in_10));
  Register #(.width(32)) register_17 (.D(in_4), .en(L4), .Q(out4), .clk(in_5), .clr(in_1));
  Register #(.width(32)) register_18 (.D(in_4), .en(L12), .Q(out12), .clk(in_5), .clr(in_1));
  Register #(.width(32)) register_19 (.D(in_4), .en(L20), .Q(out20), .clk(in_5), .clr(in_1));
  Register #(.width(32)) register_20 (.D(in_4), .en(L28), .Q(out28), .clk(in_5), .clr(in_1));
  Register #(.width(32)) register_21 (.D(in_4), .en(L5), .Q(out5), .clk(in_5), .clr(in_1));
  Register #(.width(32)) register_22 (.D(in_4), .en(L13), .Q(out13), .clk(in_5), .clr(in_1));
  Register #(.width(32)) register_23 (.D(in_4), .en(L21), .Q(out21), .clk(in_5), .clr(in_1));
  Register #(.width(32)) register_24 (.D(in_4), .en(L29), .Q(out29), .clk(in_5), .clr(in_1));
  or or_1 (or_1_out, in_3, in_7);
  Register #(.width(32)) register_25 (.D(in_4), .en(L6), .Q(out6), .clk(in_5), .clr(in_1));
  Register #(.width(32)) register_26 (.D(in_4), .en(L14), .Q(out14), .clk(in_5), .clr(in_1));
  Register #(.width(32)) register_27 (.D(in_4), .en(L22), .Q(out22), .clk(in_5), .clr(in_1));
  Register #(.width(32)) register_28 (.D(in_4), .en(L30), .Q(out30), .clk(in_5), .clr(in_1));
  and and_1 (L31, in_6, or_1_out);
  Subtractor #(.width(32)) subtractor_1 (.a(Output_3), .b(32'h4), .out(subtractor_1_out));  // open: bin, bout
  Adder #(.width(32)) adder_1 (.a(32'h4), .b(Output_3), .out(adder_1_out));  // open: cin, cout
  or or_2 (or_2_out, L31, in_1);
  Multiplexer #(.width(32), .enable("false")) multiplexer_3 (
    .in0(subtractor_1_out), .in1(adder_1_out), .out(multiplexer_3_out), .sel(in_7));
  Multiplexer #(.width(32), .enable("false")) multiplexer_4 (
    .in0(multiplexer_3_out), .in1({32{1'b1}}), .out(inputSP), .sel(in_1));
  Register #(.width(32)) register_29 (.D(in_4), .en(L7), .Q(out7), .clk(in_5), .clr(in_1));
  Register #(.width(32)) register_30 (.D(in_4), .en(L15), .Q(out15), .clk(in_5), .clr(in_1));
  Register #(.width(32)) register_31 (.D(in_4), .en(L23), .Q(out23), .clk(in_5), .clr(in_1));
  Register #(.width(32)) register_32 (.D(inputSP), .en(or_2_out), .Q(Output_3), .clk(in_5));  // open: clr

  // Other names for the same wires on the sheet: A[31:0] = Output; B[31:0] = Output_2; clock = in_5;
  //   input[31:0] = in_4; memR_W = in_6; out31[31:0] = Output_3; outA[4:0] = in_9; outB[4:0] = in_10; pop = in_7;
  //   push = in_3; reset = in_1; select[4:0] = in_8; write = in_2
endmodule

module RF_Input (
  input  [6:0] in_1,
  input  [31:0] in_2,
  input  in_3,
  input  in_4,
  input  [31:0] in_5,
  input  in_6,
  input  in_7,
  input  [31:0] in_8,
  input  in_9,
  input  in_10,
  input  in_11,
  input  [31:0] in_12,
  input  [31:0] in_13,
  output [31:0] Output
);

  wire [2:0] selector;

  or or_1 (selector[0], in_3, in_6, in_9, in_11);
  or or_2 (selector[1], in_7, in_9);
  or or_3 (selector[2], in_10, in_11);
  Multiplexer #(.select(3), .width(32), .enable("false")) multiplexer_1 (
    .in0(in_2), .in1(in_8), .in2(in_12), .in3(in_13), .in4(in_5), .in5({{25{1'b0}}, in_1}), .out(Output),
    .sel(selector));  // open: in6, in7

  // Other names for the same wires on the sheet: ALU[31:0] = in_2; HI[31:0] = in_12; isALU = in_4; isKBD = in_11;
  //   isRND = in_10; KBD[6:0] = in_1; LO[31:0] = in_13; LW = in_3; memoryA[31:0] = in_8; MFHI = in_7; MFLO = in_9;
  //   pop = in_6; RND[31:0] = in_5
endmodule

module instruction_decoder (
  output Output,
  output Output_2,
  output Output_3,
  output Output_4,
  output Output_5,
  output Output_6,
  output Output_7,
  output Output_8,
  output Output_9,
  output Output_10,
  output Output_11,
  output Output_12,
  output Output_13,
  output Output_14,
  output Output_15,
  output Output_16,
  output Output_17,
  output Output_18,
  output Output_19,
  output Output_20,
  output Output_21,
  output Output_22,
  output Output_23,
  output Output_24,
  output Output_25,
  output Output_26,
  output Output_27,
  output Output_28,
  output Output_29,
  output Output_30,
  output Output_31,
  output Output_32,
  output Output_33,
  output Output_34,
  output Output_35,
  output Output_36
);


  // Other names for the same wires on the sheet: add = Output_5; addi = Output_19; and = Output_9; andi = Output_27;
  //   beq = Output_23; bgtz = Output_31; blez = Output_28; bltz = Output_34; bne = Output_25; div = Output_17;
  //   divu = Output_21; halt = Output_26; j = Output_4; jr = Output_10; kbd = Output_35; lw = Output_36;
  //   mfhi = Output_13; mflo = Output_16; mult = Output_11; mulu = Output_14; nop = Output; nor = Output_15;
  //   or = Output_12; ori = Output_30; pop = Output_3; push = Output_7; rnd = Output_32; slt = Output_2;
  //   slti = Output_22; sltiu = Output_24; sltu = Output_6; sub = Output_8; sw = Output_20; tty = Output_29;
  //   xor = Output_18; xori = Output_33
endmodule

module tipoR (
  input  [5:0] in_1,
  input  in_2,
  output Output,
  output Output_2,
  output Output_3,
  output Output_4,
  output Output_5,
  output Output_6,
  output Output_7,
  output Output_8,
  output Output_9,
  output Output_10,
  output Output_11,
  output Output_12,
  output Output_13
);


  // Other names for the same wires on the sheet: add = Output_6; and = Output_4; div = Output_11; divu = Output_3;
  //   _0 = in_1[0]; _1 = in_1[1]; _2 = in_1[2]; _3 = in_1[3]; _4 = in_1[4]; _5 = in_1[5]; mult = Output_2;
  //   mulu = Output_7; nop = Output; nor = Output_13; or = Output_9; slt = Output_8; sltu = Output_12;
  //   sub = Output_10; xor = Output_5
endmodule
